# Fritzing sketch breadboard (saved by Fritzing 0.9.3b)
breadboards: 1

parts:
  U1 = ESP32S-HiLetgo [part_number=ESP32S-HiLetgo]
  U2 = LCD-16X2 [package=lcd-16x2_noholes]
  R1 = Resistor [tolerance=±5% resistance=220 package="0805 [SMD]"]
  S1 = Pushbutton [package="[SMD]"]
  Composant1 = Breakout Board for Electret Microphone

nets:
  N1: U1.3.3, Composant1.AUD
  N2: U1.GPIO32, Composant1.VCC
  GND: U1.GND, U2.VSS, U2.R_W, U2.K, R1.Pin_0, Composant1.GND
  VIN: U1.VIN, U2.VDD, U2.A, S1.Pin_1, S1.Pin_2
  N3: U1.GPIO15, U2.RS
  N4: U1.GPIO2, U2.E
  N5: U1.GPIO0, U2.DB4
  N6: U1.GPIO4, U2.DB5
  N7: U1.GPIO16, U2.DB6
  N8: U1.GPIO17, U2.DB7
  N9: U1.GPIO23, S1.Pin_3, S1.Pin_4

custom parts:
  ESP32S-HiLetgo: HiLetgo ESP-WROOM-32 ESP32 ESP-32S Development Board 2.4GHz Dual-Mode WiFi + Bluetooth Dual Cores Microcontroller The ESP32 integrated with Antenna switches, RF Balun, power amplifiers, low-noise amplifiers, filters, and management modules, and the entire solution occupies the least area of PCB. 2.4 GHz Wi-Fi plus Bluetooth dual-mode chip, with TSMC Ultra-low power consumption 40nm technology,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
